# Fritzing sketch sketch (saved by Fritzing 0.9.3b)
breadboards: 1

parts:
  Componente1 = Arduino Uno (Rev3) - ICSP
  LED1 = LED - 5mm [color="Red (633nm)" package="5 mm [THT]"]
  R1 = Resistor [tolerance=±5% resistance=220 package="1206 [SMD]"]
  LED2 = LED - 5mm [color="Green (565nm)" package="5 mm [THT]"]
  LED3 = LED - 5mm [color="Yellow (585nm)" package="5 mm [THT]"]
  R2 = Resistor [tolerance=±5% resistance=220 package="1206 [SMD]"]
  R3 = Resistor [tolerance=±5% resistance=220 package="1206 [SMD]"]
  S1 = Pushbutton [package="[THT]"]

nets:
  N1: Componente1.GND, R1.Pin_1, R2.Pin_1, R3.Pin_1
  N2: Componente1.D2, LED1.anode
  N3: Componente1.D3_PWM, LED3.anode
  N4: Componente1.D4, LED2.anode
  N5: LED1.cathode, R1.Pin_0
  N6: LED2.cathode, R2.Pin_0
  N7: LED3.cathode, R3.Pin_0
  N8: S1.Pin_1, S1.Pin_2
  N9: S1.Pin_3, S1.Pin_4
